# Fritzing sketch DHT11 (saved by Fritzing 0.9.3b)
breadboards: 1

parts:
  RHT1 = Humidity and Temperature Sensor RHT03
  WeMos_D1_Mini1 = WeMos D1 Mini
  R1 = Resistor [tolerance=±5% resistance=220 package="2010 [SMD]"]

nets:
  VCC: RHT1.Vcc, WeMos_D1_Mini1.3V3, R1.Pin_0
  N1: RHT1.Data-signal, WeMos_D1_Mini1.D2, R1.Pin_1
  N2: RHT1.GND_1, RHT1.GND_2, WeMos_D1_Mini1.G
