# Fritzing sketch UN_Sensor_Sketch (saved by Fritzing 0.9.3b)
breadboards: 1

parts:
  Part1 = GUVA-S12SD UV Light Sensor
  WeMos_D1_Mini2 = WeMos D1 Mini

nets:
  N1: Part1.Out, WeMos_D1_Mini2.A0
  N2: Part1.GND, WeMos_D1_Mini2.G

custom parts:
  GUVA-S12SD UV Light Sensor: Extend your light-sensing spectrum with this analog UV sensor module. It uses a UV photodiode, which can detect the 240-370nm range of light (which covers UVB and most of UVA spectrum). The signal level from the photodiode is very small, in the nano-ampere level, so we tossed on an opamp to amplify the signal to a more manageable volt-level.
