# Fritzing sketch ccs811 (saved by Fritzing 0.9.3b)
breadboards: 1

parts:
  Part1 = Adafruit CCS811
  WeMos_D1_Mini1 = WeMos D1 Mini

nets:
  3.3V: Part1.3.3V, WeMos_D1_Mini1.3V3
  N1: Part1.GND, Part1.!WAKE, WeMos_D1_Mini1.G
  N2: Part1.SDA, WeMos_D1_Mini1.D2
  N3: Part1.SCL, WeMos_D1_Mini1.D1
